# Fritzing sketch Nano Sun Tracker - rev B (saved by Fritzing 0.9.10b)
breadboards: 1

parts:
  Nano = Arduino Nano (Rev3.0)
  BottomLeft = PHOTOCELL [package=photocell-kit]
  Azimuth = Basic Servo
  Elevation = Basic Servo
  TopLeft = PHOTOCELL [package=photocell-kit]
  TopRight = PHOTOCELL [package=photocell-kit]
  BottomRight = PHOTOCELL [package=photocell-kit]
  BR-R4 = Resistor [tolerance=±5% resistance=10k power=0.25 package=THT]
  BL-R3 = Resistor [tolerance=±5% resistance=10k power=0.25 package=THT]
  TL-R1 = Resistor [tolerance=±5% resistance=10k power=0.25 package=THT]
  TR-R2 = Resistor [tolerance=±5% resistance=10k power=0.25 package=THT]

nets:
  GND: Nano.GND, Azimuth.gnd, Elevation.gnd, BR-R4.Pin_1, BL-R3.Pin_0, TL-R1.Pin_0, TR-R2.Pin_1
  N1: Nano.D3, Elevation.pulse
  N2: Nano.D10, Azimuth.pulse
  VCC: Nano.5V, BottomLeft.P$2, Azimuth.vcc, Elevation.vcc, TopLeft.P$2, TopRight.P$1, BottomRight.P$1
  N3: Nano.A3, BottomRight.P$2, BR-R4.Pin_0
  N4: Nano.A2, BottomLeft.P$1, BL-R3.Pin_1
  N5: Nano.A1, TopRight.P$2, TR-R2.Pin_0
  N6: Nano.A0, TopLeft.P$1, TL-R1.Pin_1
