# Fritzing sketch Nano Sun Tracker (saved by Fritzing 0.9.4)
breadboards: 1

parts:
  Part1 = Arduino Nano (Rev3.0)
  PWM1 = PCA9685 16x12-bit PWM Breakout
  R1 = PHOTOCELL [package=photocell-kit]
  Azimuth = Basic Servo
  Elevation = Basic Servo
  R2 = PHOTOCELL [package=photocell-kit]
  R3 = PHOTOCELL [package=photocell-kit]
  R4 = PHOTOCELL [package=photocell-kit]
  R5 = Resistor [tolerance=±5% resistance=10k package=THT]
  R6 = Resistor [tolerance=±5% resistance=10k package=THT]
  R7 = Resistor [tolerance=±5% resistance=10k package=THT]
  R8 = Resistor [tolerance=±5% resistance=10k package=THT]

nets:
  N1: Part1.A5, PWM1.no_name_yet#503
  N2: Part1.A4, PWM1.no_name_yet#504
  N3: Part1.A3, R4.P$2, R5.Pin_0
  N4: Part1.A2, R1.P$1, R6.Pin_1
  N5: Part1.A1, R3.P$2, R8.Pin_0
  N6: Part1.A0, R2.P$1, R7.Pin_1
  N7: Part1.3V3, PWM1.no_name_yet#505
  N8: PWM1.no_name_yet#0, Azimuth.pulse
  N9: PWM1.no_name_yet#1, Elevation.pulse
  N10: PWM1.no_name_yet#100, PWM1.no_name_yet#101, PWM1.no_name_yet#506, R1.P$2, R2.P$2, R3.P$1, R4.P$1
  N11: PWM1.no_name_yet#501, PWM1.no_name_yet#1000, PWM1.no_name_yet#1001, R5.Pin_1, R6.Pin_0, R7.Pin_0, R8.Pin_1
